# Fritzing sketch bGeigieNanoKit (saved by Fritzing 0.7.6b)

parts:
  GPS1 = Adafruit Ultimate GPS Breakout
  Arduino1 = Arduino Fio
  Li-ion_Battery_3_7V1 = Battery
  Part1 = OpenLog
  OLED2 = 128x32 SPI Monochrome OLEDDisplay

nets:
  N1: GPS1.FIX, GPS1.TX, Arduino1.D8
  N2: GPS1.RX, Arduino1.D9
  GND: GPS1.GND, Arduino1.GND, Part1.GND, OLED2.GND
  VIN: GPS1.VIN, Arduino1.3V3, Part1.VCC, OLED2.3.3Vo
  N3: Arduino1.D3, OLED2.RST
  N4: Arduino1.D4, OLED2.CS
  N5: Arduino1.D5, OLED2.D/C
  N6: Arduino1.D6, OLED2.DATA
  N7: Arduino1.D7, OLED2.CLK
  N8: Arduino1.D10, Part1.TXO
  N9: Arduino1.D11, Part1.RXI
  N10: Arduino1.D12, Part1.DTR
  N11: Arduino1.lipo+, Li-ion_Battery_3_7V1.aún_sin_nombre#0
  N12: Arduino1.lipo-, Li-ion_Battery_3_7V1.aún_sin_nombre#1

notes:
  Medcom iRover HV
  with LND7317

custom parts:
  Arduino Fio: The Arduino Fio is a microcontroller board based on the ATmega328P runs at 3.3V and 8 MHz. It has 14 digital input/output pins (of which 6 can be used as PWM outputs), 8 analog inputs, an on-board resonator, a reset button, and holes for mounting pin headers. It has connections for a Lithium Polymer battery and includes a charge circuit over USB. An XBee socket is available on the bottom of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
  128x32 SPI Monochrome OLEDDisplay: 128x32 SPI OLED Monochrome Display
